// Logisim project Matheus Endlich Silveira- MCU_4bits_CC3MB_24.circ as structural Verilog
module Main (
  input  [3:0] A,
  input  [3:0] B,
  input  [2:0] \Operações ,
  output Overflow,
  output Overflow_2,
  output [3:0] Saida
);

  wire decoder_1_s0, decoder_1_s1, decoder_1_s2, decoder_1_s4;
  wire [3:0] add_4_1_out_5, sub_4_1_out_5;

  Decoder decoder_1 (
    .A_B_C(\Operações ), .S0(decoder_1_s0), .S1(decoder_1_s1), .S2(decoder_1_s2), .S4(decoder_1_s4));  // open: S3, S5, S6, S7
  Buffer buffer_1 (.B(B), .in_2(decoder_1_s0), .Saida(Saida));
  Add_4 add_4_1 (.in_2(A), .Vem_1(Overflow), .in_1(B), .Vem__1(1'b0), .out_5(add_4_1_out_5));
  Buffer buffer_2 (.B(add_4_1_out_5), .in_2(decoder_1_s1), .Saida(Saida));
  Sub_4 sub_4_1 (.A(A), .Overflow(Overflow_2), .B(B), .Vem_1(1'b0), .out_5(sub_4_1_out_5));
  Buffer buffer_3 (.B(sub_4_1_out_5), .in_2(decoder_1_s2), .Saida(Saida));
  Buffer_N buffer_n_1 (.B(B), .in_2(decoder_1_s4), .Saida(Saida));
endmodule

module Add_1 (
  input  A,
  input  B,
  input  Vem_1,
  output Saida,
  output Vai_1
);

  wire and_1_out, and_2_out, or_1_out, xor_1_out;

  xor xor_1 (xor_1_out, A, B);
  or or_1 (or_1_out, B, Vem_1);
  xor xor_2 (Saida, xor_1_out, Vem_1);
  and and_1 (and_1_out, or_1_out, A);
  and and_2 (and_2_out, B, Vem_1);
  or or_2 (Vai_1, and_1_out, and_2_out);
endmodule

module Add_4 (
  input  [3:0] in_1,
  input  [3:0] in_2,
  input  Vem__1,
  output Vem_1,
  output [3:0] out_5
);

  wire add_1_2_vai_1, add_1_3_vai_1, add_1_4_vai_1;

  Add_1 add_1_1 (.A(in_2[3]), .B(in_1[3]), .Vem_1(add_1_2_vai_1), .Saida(out_5[3]), .Vai_1(Vem_1));
  Add_1 add_1_2 (.A(in_2[2]), .B(in_1[2]), .Vem_1(add_1_3_vai_1), .Saida(out_5[2]), .Vai_1(add_1_2_vai_1));
  Add_1 add_1_3 (.A(in_2[1]), .B(in_1[1]), .Vem_1(add_1_4_vai_1), .Saida(out_5[1]), .Vai_1(add_1_3_vai_1));
  Add_1 add_1_4 (.A(in_2[0]), .B(in_1[0]), .Vem_1(Vem__1), .Saida(out_5[0]), .Vai_1(add_1_4_vai_1));
endmodule

module Sub_1 (
  input  A,
  input  B,
  input  Vem_1,
  output Saida,
  output Vai_1
);

  wire and_1_out, and_2_out, not_1_out, or_1_out, xor_1_out;

  not not_1 (not_1_out, A);
  xor xor_1 (xor_1_out, A, B);
  or or_1 (or_1_out, B, Vem_1);
  xor xor_2 (Saida, xor_1_out, Vem_1);
  and and_1 (and_1_out, or_1_out, not_1_out);
  and and_2 (and_2_out, B, Vem_1);
  or or_2 (Vai_1, and_1_out, and_2_out);
endmodule

module Sub_4 (
  input  [3:0] B,
  input  [3:0] A,
  input  Vem_1,
  output Overflow,
  output [3:0] out_5
);

  wire sub_1_2_vai_1, sub_1_3_vai_1, sub_1_4_vai_1;

  Sub_1 sub_1_1 (.A(A[3]), .B(B[3]), .Vem_1(sub_1_2_vai_1), .Saida(out_5[3]), .Vai_1(Overflow));
  Sub_1 sub_1_2 (.A(A[2]), .B(B[2]), .Vem_1(sub_1_3_vai_1), .Saida(out_5[2]), .Vai_1(sub_1_2_vai_1));
  Sub_1 sub_1_3 (.A(A[1]), .B(B[1]), .Vem_1(sub_1_4_vai_1), .Saida(out_5[1]), .Vai_1(sub_1_3_vai_1));
  Sub_1 sub_1_4 (.A(A[0]), .B(B[0]), .Vem_1(Vem_1), .Saida(out_5[0]), .Vai_1(sub_1_4_vai_1));
endmodule

module Buffer (
  input  [3:0] B,
  input  in_2,
  output [3:0] Saida
);

  assign Saida[3] = in_2 ? B[3] : 1'bz;  // Controlled_Buffer controlled_buffer_1
  assign Saida[2] = in_2 ? B[2] : 1'bz;  // Controlled_Buffer controlled_buffer_2
  assign Saida[0] = in_2 ? B[0] : 1'bz;  // Controlled_Buffer controlled_buffer_3
  assign Saida[1] = in_2 ? B[1] : 1'bz;  // Controlled_Buffer controlled_buffer_4
endmodule

module Buffer_N (
  input  [3:0] B,
  input  in_2,
  output [3:0] Saida
);

  assign Saida[2] = in_2 ? ~B[2] : 1'bz;  // Controlled_Inverter controlled_inverter_1
  assign Saida[3] = in_2 ? ~B[3] : 1'bz;  // Controlled_Inverter controlled_inverter_2
  assign Saida[0] = in_2 ? ~B[0] : 1'bz;  // Controlled_Inverter controlled_inverter_3
  assign Saida[1] = in_2 ? ~B[1] : 1'bz;  // Controlled_Inverter controlled_inverter_4
endmodule

module Decoder (
  input  [2:0] A_B_C,
  output S0,
  output S1,
  output S2,
  output S3,
  output S4,
  output S5,
  output S6,
  output S7
);

  wire not_1_out, not_2_out, not_3_out, not_4_out, not_5_out, not_6_out, not_7_out, not_8_out, not_9_out,
       not_10_out, not_11_out, not_12_out;

  not not_1 (not_1_out, A_B_C[2]);
  not not_2 (not_2_out, A_B_C[1]);
  not not_3 (not_3_out, A_B_C[0]);
  not not_4 (not_4_out, A_B_C[2]);
  not not_5 (not_5_out, A_B_C[1]);
  not not_6 (not_6_out, A_B_C[2]);
  not not_7 (not_7_out, A_B_C[0]);
  not not_8 (not_8_out, A_B_C[2]);
  not not_9 (not_9_out, A_B_C[1]);
  not not_10 (not_10_out, A_B_C[0]);
  not not_11 (not_11_out, A_B_C[1]);
  not not_12 (not_12_out, A_B_C[0]);
  and and_1 (S7, A_B_C[2], A_B_C[1], A_B_C[0]);
  and and_2 (S0, not_1_out, not_2_out, not_3_out);
  and and_3 (S1, not_4_out, not_5_out, A_B_C[0]);
  and and_4 (S2, not_6_out, A_B_C[1], not_7_out);
  and and_5 (S3, not_8_out, A_B_C[1], A_B_C[0]);
  and and_6 (S4, A_B_C[2], not_9_out, not_10_out);
  and and_7 (S5, A_B_C[2], not_11_out, A_B_C[0]);
  and and_8 (S6, A_B_C[2], A_B_C[1], not_12_out);
endmodule
